// Logisim project counter.circ as structural Verilog: 1 circuit, main circuit counter
module counter (
  input  [15:0] target_score,
  input  increment,
  input  zero,
  output [3:0] out_4,
  output [3:0] out_5,
  output [3:0] out_6,
  output victory
);

  wire comparator_2_eq, comparator_3_eq, comparator_4_eq, or_1_out, or_2_out, or_3_out;
  wire [15:0] counter_1_q;

  Counter #(.width(16), .max('hffff)) counter_1 (
    .count(1'b1), .Q(counter_1_q), .clk(increment));  // open: load, D, carry, clr
  Pull_Resistor pull_resistor_1 (.node(increment));
  Pull_Resistor pull_resistor_2 (.node(zero));
  Comparator #(.width(16)) comparator_1 (.a(target_score), .b(counter_1_q), .eq(victory));  // open: gt, lt
  Counter #(.width(4), .max('hf)) counter_2 (
    .count(1'b1), .Q(out_6), .clk(increment), .clr(or_1_out));  // open: load, D, carry
  or or_1 (or_1_out, zero, comparator_2_eq);
  Comparator #(.width(4)) comparator_2 (.a(out_6), .b(4'b1010), .eq(comparator_2_eq));  // open: gt, lt
  Counter #(.width(4), .max('hf)) counter_3 (
    .count(1'b1), .Q(out_5), .clk(comparator_2_eq), .clr(or_2_out));  // open: load, D, carry
  or or_2 (or_2_out, zero, comparator_3_eq);
  Comparator #(.width(4)) comparator_3 (.a(out_5), .b(4'b1010), .eq(comparator_3_eq));  // open: gt, lt
  Counter #(.width(4), .max('hf)) counter_4 (
    .count(1'b1), .Q(out_4), .clk(comparator_3_eq), .clr(or_3_out));  // open: load, D, carry
  or or_3 (or_3_out, zero, comparator_4_eq);
  Comparator #(.width(4)) comparator_4 (.a(out_4), .b(4'b1010), .eq(comparator_4_eq));  // open: gt, lt

  // Other names for the same wires on the sheet: digit1[3:0] = out_6; digit2[3:0] = out_5; digit3[3:0] = out_4
endmodule
