// Logisim project display-controller.circ as structural Verilog: 2 circuits, main circuit display_controller
module display_controller (
  input  [3:0] X_coord,
  input  [3:0] Y_coord,
  input  pixel_state,
  input  write,
  input  pixel_check,
  input  game_over,
  input  victory,
  input  req_rand,
  output [15:0] c00,
  output [15:0] c01,
  output [15:0] c02,
  output [7:0] food,
  output [15:0] c03,
  output [15:0] c04,
  output checked,
  output [15:0] c05,
  output [15:0] c06,
  output [15:0] c07,
  output [15:0] c08,
  output [15:0] c09,
  output [15:0] c10,
  output [15:0] c11,
  output [15:0] c12,
  output [15:0] c13,
  output [15:0] c14,
  output [15:0] c15
);

  wire and_1_out, and_2_out, and_3_out, and_20_out, and_21_out, and_22_out, and_23_out, and_24_out,
       and_25_out, and_26_out, and_27_out, and_28_out, and_29_out, and_30_out, and_31_out, and_32_out,
       and_33_out, and_34_out, and_35_out, and_36_out, and_37_out, and_38_out, and_39_out, and_40_out,
       and_41_out, and_42_out, and_43_out, and_44_out, and_45_out, and_46_out, and_47_out, and_48_out,
       and_49_out, and_50_out, and_51_out, check, clock_1_out, comparator_1_gt, not_1_out, not_2_out,
       not_3_out, not_4_out, not_5_out, not_6_out, not_7_out, not_8_out, not_9_out, not_10_out, not_11_out,
       not_12_out, not_13_out, not_14_out, not_15_out, not_16_out, not_17_out, not_18_out, not_19_out,
       not_20_out, not_21_out, not_22_out, not_23_out, not_25_out, not_27_out, not_28_out, not_29_out,
       not_30_out, not_31_out, not_32_out, not_33_out, not_34_out, not_35_out, not_36_out, not_37_out,
       not_38_out, not_39_out, not_40_out, not_41_out, not_42_out, not_43_out, not_44_out, not_45_out,
       not_46_out, not_47_out, not_48_out, not_49_out, not_50_out, not_51_out, not_52_out, not_53_out,
       not_54_out, not_55_out, not_56_out, not_57_out, not_58_out, not_59_out, not_60_out, not_61_out,
       not_62_out, not_63_out, not_64_out, not_65_out, not_66_out, not_67_out, not_68_out, not_69_out,
       not_70_out, not_71_out, not_72_out, not_73_out, not_74_out, or_1_out, or_2_out, or_3_out, or_4_out,
       start, t_ff_1_q, t_ff_1_qn, wrt0, wrt1, wrt2, wrt3, wrt4, wrt5, wrt6, wrt7, wrt8, wrt9, wrt10, wrt11,
       wrt12, wrt13, wrt14, wrt15;
  wire [3:0] controlled_buffer_2_out, controlled_buffer_4_out;
  wire [7:0] counter_1_q;
  wire [15:0] and_4_out, and_5_out, and_6_out, and_7_out, and_8_out, and_9_out, and_10_out, and_11_out,
       and_12_out, and_13_out, and_14_out, and_15_out, and_16_out, and_17_out, and_18_out, and_19_out,
       and_52_out, and_53_out, and_54_out, and_55_out, and_56_out, and_57_out, and_58_out, and_59_out,
       and_60_out, and_61_out, and_62_out, and_63_out, and_64_out, and_65_out, and_66_out, and_67_out, beg00,
       beg01, beg02, beg03, beg04, beg05, beg06, beg07, beg08, beg09, beg10, beg11, beg12, beg13, beg14,
       beg15, checked_value, controlled_buffer_7_out, controlled_buffer_10_out, controlled_buffer_13_out,
       controlled_buffer_16_out, controlled_buffer_19_out, controlled_buffer_22_out,
       controlled_buffer_25_out, controlled_buffer_28_out, controlled_buffer_31_out,
       controlled_buffer_34_out, controlled_buffer_37_out, controlled_buffer_40_out,
       controlled_buffer_43_out, controlled_buffer_46_out, controlled_buffer_49_out,
       controlled_buffer_52_out, controlled_buffer_55_out, controlled_buffer_57_out,
       controlled_buffer_59_out, controlled_buffer_61_out, controlled_buffer_63_out,
       controlled_buffer_65_out, controlled_buffer_67_out, controlled_buffer_69_out,
       controlled_buffer_71_out, controlled_buffer_73_out, controlled_buffer_75_out,
       controlled_buffer_77_out, controlled_buffer_79_out, controlled_buffer_81_out,
       controlled_buffer_83_out, controlled_buffer_85_out, demultiplexer_3_out0, end00, end01, end02, end03,
       end04, end05, end06, end07, end08, end09, end10, end11, end12, end13, end14, end15, mask, or_6_out,
       or_7_out, or_8_out, or_9_out, or_10_out, or_11_out, or_12_out, or_13_out, or_14_out, or_15_out,
       or_16_out, or_17_out, or_18_out, or_19_out, or_20_out, or_21_out, register_1_q, register_2_q,
       register_3_q, register_4_q, register_5_q, register_6_q, register_7_q, register_8_q, register_9_q,
       register_10_q, register_11_q, register_12_q, register_13_q, register_14_q, register_15_q,
       register_16_q, value, win00, win01, win02, win03, win04, win05, win06, win07, win08, win09, win10,
       win11, win12, win13, win14, win15;

  // Probe on 8'ha0
  // Probe on 8'ha0
  // Probe on 8'ha7
  // Probe on 8'ha8
  // Probe on 8'ha6
  // Probe on 8'ha8
  // Probe on 8'ha7
  // Probe on 8'ha0
  // Probe on 8'haf
  // Probe on 8'ha0
  // Probe on 8'haf
  // Probe on 8'ha2
  // Probe on 8'ha4
  // Probe on 8'haf
  // Probe on 8'ha0
  // Probe on 8'ha0
  not not_1 (not_1_out, and_1_out);
  and and_1 (and_1_out, checked, not_8_out);
  // Probe on 8'h7f
  // Probe on 8'h7f
  // Probe on 8'h73
  // Probe on 8'h4f
  // Probe on 8'h73
  // Probe on 8'h7f
  // Probe on 8'h67
  // Probe on 8'h5b
  // Probe on 8'h67
  // Probe on 8'h7f
  // Probe on 8'h63
  // Probe on 8'h5f
  // Probe on 8'h5f
  // Probe on 8'h63
  // Probe on 8'h7f
  // Probe on 8'h7f
  and and_2 (and_2_out, req_rand, not_1_out);
  not not_2 (not_2_out, comparator_1_gt);
  Counter counter_1 (.load(1'b0), .count(1'b1), .Q(counter_1_q), .clk(not_8_out), .clr(not_3_out));  // open: D, carry
  not not_3 (not_3_out, req_rand);
  reverser reverser_1 (.in(16'ha07f), .reversed(win00));
  reverser reverser_2 (.in(16'ha07f), .reversed(win01));
  reverser reverser_3 (.in(16'ha773), .reversed(win02));
  reverser reverser_4 (.in(16'ha84f), .reversed(win03));
  reverser reverser_5 (.in(16'ha673), .reversed(win04));
  reverser reverser_6 (.in(16'ha87f), .reversed(win05));
  reverser reverser_7 (.in(16'ha767), .reversed(win06));
  reverser reverser_8 (.in(16'ha05b), .reversed(win07));
  reverser reverser_9 (.in(16'haf67), .reversed(win08));
  reverser reverser_10 (.in(16'ha07f), .reversed(win09));
  reverser reverser_11 (.in(16'haf63), .reversed(win10));
  reverser reverser_12 (.in(16'ha25f), .reversed(win11));
  reverser reverser_13 (.in(16'ha45f), .reversed(win12));
  reverser reverser_14 (.in(16'haf63), .reversed(win13));
  reverser reverser_15 (.in(16'ha07f), .reversed(win14));
  reverser reverser_16 (.in(16'ha07f), .reversed(win15));
  Random random_1 (.clk(and_3_out), .next(1'b1), .out(food));  // open: clr
  and and_3 (and_3_out, and_2_out, not_2_out);
  not not_4 (not_4_out, and_3_out);
  not not_5 (not_5_out, not_4_out);
  not not_6 (not_6_out, not_7_out);
  not not_7 (not_7_out, not_15_out);
  not not_8 (not_8_out, not_6_out);
  Comparator comparator_1 (.a(counter_1_q), .b(8'h18), .gt(comparator_1_gt));  // open: eq, lt
  not not_9 (not_9_out, not_11_out);
  not not_10 (not_10_out, not_12_out);
  not not_11 (not_11_out, not_5_out);
  not not_12 (not_12_out, not_9_out);
  not not_13 (not_13_out, not_14_out);
  not not_14 (not_14_out, not_10_out);
  not not_15 (not_15_out, not_13_out);
  // Probe on {8{1'b0}}
  // Probe on 8'h1f
  // Probe on 8'h44
  // Probe on 8'h4a
  // Probe on 8'hd1
  // Probe on 8'h80
  // Probe on 8'hdf
  // Probe on 8'h55
  // Probe on 8'h55
  // Probe on 8'hc0
  // Probe on 8'h80
  // Probe on 8'h97
  // Probe on 8'hc0
  // Probe on 8'h5c
  // Probe on 8'h76
  // Probe on {8{1'b0}}
  // Probe on {8{1'b0}}
  // Probe on 8'h24
  // Probe on 8'h2a
  // Probe on 8'h2a
  // Probe on 8'h12
  // Probe on {8{1'b0}}
  // Probe on 8'h3e
  // Probe on 8'h4
  // Probe on 8'h8
  // Probe on 8'h3e
  // Probe on {8{1'b0}}
  // Probe on 8'h3c
  // Probe on 8'h12
  // Probe on 8'h3c
  // Probe on 8'h80
  // Probe on {8{1'b0}}
  not not_16 (not_16_out, req_rand);
  assign check = not_16_out ? pixel_check : 1'bz;  // Controlled_Buffer controlled_buffer_1
  reverser reverser_17 (.in({16{1'b0}}), .reversed(beg00));
  reverser reverser_18 (.in(16'h1f24), .reversed(beg01));
  reverser reverser_19 (.in(16'h442a), .reversed(beg02));
  reverser reverser_20 (.in(16'h4a2a), .reversed(beg03));
  reverser reverser_21 (.in(16'hd112), .reversed(beg04));
  reverser reverser_22 (.in(16'h8000), .reversed(beg05));
  reverser reverser_23 (.in(16'hdf3e), .reversed(beg06));
  reverser reverser_24 (.in(16'h5504), .reversed(beg07));
  reverser reverser_25 (.in(16'h5508), .reversed(beg08));
  reverser reverser_26 (.in(16'hc03e), .reversed(beg09));
  reverser reverser_27 (.in(16'h8000), .reversed(beg10));
  reverser reverser_28 (.in(16'h973c), .reversed(beg11));
  reverser reverser_29 (.in(16'hc012), .reversed(beg12));
  reverser reverser_30 (.in(16'h5c3c), .reversed(beg13));
  reverser reverser_31 (.in(16'h7680), .reversed(beg14));
  reverser reverser_32 (.in({16{1'b0}}), .reversed(beg15));
  not not_17 (not_17_out, req_rand);
  assign controlled_buffer_2_out = not_17_out ? Y_coord : 4'bz;  // Controlled_Buffer controlled_buffer_2
  not not_18 (not_18_out, not_19_out);
  not not_19 (not_19_out, req_rand);
  assign check = req_rand ? not_18_out : 1'bz;  // Controlled_Buffer controlled_buffer_3
  Clock clock_1 (.out(clock_1_out));
  not not_20 (not_20_out, req_rand);
  not not_21 (not_21_out, req_rand);
  assign controlled_buffer_4_out = not_21_out ? X_coord : 4'bz;  // Controlled_Buffer controlled_buffer_4
  not not_22 (not_22_out, not_23_out);
  not not_23 (not_23_out, req_rand);
  assign controlled_buffer_2_out = not_22_out ? food[7:4] : 4'bz;  // Controlled_Buffer controlled_buffer_5
  Pull_Resistor pull_resistor_1 (.node(check));
  or or_1 (or_1_out, check, write);
  not not_24 (start, t_ff_1_q);
  T_Flip_Flop t_ff_1 (.clk(clock_1_out), .T(t_ff_1_qn), .Q(t_ff_1_q), .Qn(t_ff_1_qn));  // open: preset, reset, en
  not not_25 (not_25_out, not_20_out);
  assign controlled_buffer_4_out = not_25_out ? food[3:0] : 4'bz;  // Controlled_Buffer controlled_buffer_6
  Pull_Resistor pull_resistor_2 (.node(controlled_buffer_4_out));
  Demultiplexer #(.select(4)) demultiplexer_1 (
    .out0(wrt0), .out1(wrt1), .out2(wrt2), .out3(wrt3), .out4(wrt4), .out5(wrt5), .out6(wrt6), .out7(wrt7),
    .out8(wrt8), .out9(wrt9), .out10(wrt10), .out11(wrt11), .out12(wrt12), .out13(wrt13), .out14(wrt14),
    .out15(wrt15), .in(or_1_out), .sel(controlled_buffer_4_out));  // open: en
  // Probe on 8'h1c
  // Probe on 8'h22
  // Probe on 8'h22
  // Probe on 8'h1c
  // Probe on {8{1'b0}}
  // Probe on 8'h1e
  // Probe on 8'h20
  // Probe on 8'h1e
  // Probe on {8{1'b0}}
  // Probe on 8'h3e
  // Probe on 8'h2a
  // Probe on {8{1'b0}}
  // Probe on 8'h3e
  // Probe on 8'ha
  // Probe on 8'ha
  // Probe on 8'h34
  Pull_Resistor pull_resistor_3 (.node(controlled_buffer_2_out));
  or or_2 (or_2_out, pixel_state, check);
  Demultiplexer #(.select(4)) demultiplexer_2 (
    .out0(value[0]), .out1(value[1]), .out2(value[2]), .out3(value[3]), .out4(value[4]), .out5(value[5]),
    .out6(value[6]), .out7(value[7]), .out8(value[8]), .out9(value[9]), .out10(value[10]), .out11(value[11]),
    .out12(value[12]), .out13(value[13]), .out14(value[14]), .out15(value[15]), .in(or_2_out),
    .sel(controlled_buffer_2_out));  // open: en
  Demultiplexer #(.select(4)) demultiplexer_3 (
    .out0(demultiplexer_3_out0[0]), .out1(demultiplexer_3_out0[1]), .out2(demultiplexer_3_out0[2]),
    .out3(demultiplexer_3_out0[3]), .out4(demultiplexer_3_out0[4]), .out5(demultiplexer_3_out0[5]),
    .out6(demultiplexer_3_out0[6]), .out7(demultiplexer_3_out0[7]), .out8(demultiplexer_3_out0[8]),
    .out9(demultiplexer_3_out0[9]), .out10(demultiplexer_3_out0[10]), .out11(demultiplexer_3_out0[11]),
    .out12(demultiplexer_3_out0[12]), .out13(demultiplexer_3_out0[13]), .out14(demultiplexer_3_out0[14]),
    .out15(demultiplexer_3_out0[15]), .in(1'b1), .sel(controlled_buffer_2_out));  // open: en
  or or_3 (or_3_out, checked_value[0], checked_value[1], checked_value[2], checked_value[3], checked_value[4], checked_value[5], checked_value[6]);
  or or_4 (or_4_out, checked_value[7], checked_value[8], checked_value[9], checked_value[10], checked_value[11], checked_value[12], checked_value[13]);
  // Probe on 8'h38
  // Probe on 8'h44
  // Probe on 8'h64
  // Probe on {8{1'b0}}
  // Probe on 8'h78
  // Probe on 8'h24
  // Probe on 8'h78
  // Probe on {8{1'b0}}
  // Probe on 8'h7c
  // Probe on 8'h8
  // Probe on 8'h10
  // Probe on 8'h8
  // Probe on 8'h7c
  // Probe on {8{1'b0}}
  // Probe on 8'h7c
  // Probe on 8'h54
  or or_5 (checked, or_3_out, or_4_out, checked_value[14], checked_value[15]);
  reverser reverser_33 (.in(16'h1c38), .reversed(end00));
  reverser reverser_34 (.in(16'h2244), .reversed(end01));
  reverser reverser_35 (.in(16'h2264), .reversed(end02));
  reverser reverser_36 (.in(16'h1c00), .reversed(end03));
  reverser reverser_37 (.in(16'h78), .reversed(end04));
  reverser reverser_38 (.in(16'h1e24), .reversed(end05));
  reverser reverser_39 (.in(16'h2078), .reversed(end06));
  reverser reverser_40 (.in(16'h1e00), .reversed(end07));
  reverser reverser_41 (.in(16'h7c), .reversed(end08));
  reverser reverser_42 (.in(16'h3e08), .reversed(end09));
  reverser reverser_43 (.in(16'h2a10), .reversed(end10));
  reverser reverser_44 (.in(16'h8), .reversed(end11));
  reverser reverser_45 (.in(16'h3e7c), .reversed(end12));
  reverser reverser_46 (.in(16'ha00), .reversed(end13));
  reverser reverser_47 (.in(16'ha7c), .reversed(end14));
  reverser reverser_48 (.in(16'h3454), .reversed(end15));
  // Probe on value
  // Probe on mask
  assign mask = ~demultiplexer_3_out0;  // NOT_Gate not_26, 16 bits wide
  assign and_4_out = register_1_q & mask;  // AND_Gate and_4, 16 bits wide
  assign and_5_out = register_2_q & mask;  // AND_Gate and_5, 16 bits wide
  assign and_6_out = register_3_q & mask;  // AND_Gate and_6, 16 bits wide
  assign and_7_out = register_4_q & mask;  // AND_Gate and_7, 16 bits wide
  assign and_8_out = register_5_q & mask;  // AND_Gate and_8, 16 bits wide
  assign and_9_out = register_6_q & mask;  // AND_Gate and_9, 16 bits wide
  assign and_10_out = register_7_q & mask;  // AND_Gate and_10, 16 bits wide
  assign and_11_out = register_8_q & mask;  // AND_Gate and_11, 16 bits wide
  assign and_12_out = register_9_q & mask;  // AND_Gate and_12, 16 bits wide
  assign and_13_out = register_10_q & mask;  // AND_Gate and_13, 16 bits wide
  assign and_14_out = register_11_q & mask;  // AND_Gate and_14, 16 bits wide
  assign and_15_out = register_12_q & mask;  // AND_Gate and_15, 16 bits wide
  assign and_16_out = register_13_q & mask;  // AND_Gate and_16, 16 bits wide
  assign and_17_out = register_14_q & mask;  // AND_Gate and_17, 16 bits wide
  assign and_18_out = register_15_q & mask;  // AND_Gate and_18, 16 bits wide
  assign and_19_out = register_16_q & mask;  // AND_Gate and_19, 16 bits wide
  assign or_6_out = value | and_4_out;  // OR_Gate or_6, 16 bits wide
  Register #(.width(16)) register_1 (.D(or_6_out), .Q(register_1_q), .clk(and_20_out));  // open: en, clr
  and and_20 (and_20_out, write, wrt0);
  Register #(.width(16)) register_2 (.D(or_7_out), .Q(register_2_q), .clk(and_21_out));  // open: en, clr
  assign or_7_out = value | and_5_out;  // OR_Gate or_7, 16 bits wide
  and and_21 (and_21_out, write, wrt1);
  assign or_8_out = value | and_6_out;  // OR_Gate or_8, 16 bits wide
  Register #(.width(16)) register_3 (.D(or_8_out), .Q(register_3_q), .clk(and_22_out));  // open: en, clr
  and and_22 (and_22_out, write, wrt2);
  Register #(.width(16)) register_4 (.D(or_9_out), .Q(register_4_q), .clk(and_23_out));  // open: en, clr
  assign or_9_out = value | and_7_out;  // OR_Gate or_9, 16 bits wide
  and and_23 (and_23_out, write, wrt3);
  Register #(.width(16)) register_5 (.D(or_10_out), .Q(register_5_q), .clk(and_24_out));  // open: en, clr
  assign or_10_out = value | and_8_out;  // OR_Gate or_10, 16 bits wide
  and and_24 (and_24_out, write, wrt4);
  assign or_11_out = value | and_9_out;  // OR_Gate or_11, 16 bits wide
  Register #(.width(16)) register_6 (.D(or_11_out), .Q(register_6_q), .clk(and_25_out));  // open: en, clr
  and and_25 (and_25_out, write, wrt5);
  Register #(.width(16)) register_7 (.D(or_12_out), .Q(register_7_q), .clk(and_26_out));  // open: en, clr
  assign or_12_out = value | and_10_out;  // OR_Gate or_12, 16 bits wide
  and and_26 (and_26_out, write, wrt6);
  assign or_13_out = value | and_11_out;  // OR_Gate or_13, 16 bits wide
  Register #(.width(16)) register_8 (.D(or_13_out), .Q(register_8_q), .clk(and_27_out));  // open: en, clr
  and and_27 (and_27_out, write, wrt7);
  Register #(.width(16)) register_9 (.D(or_14_out), .Q(register_9_q), .clk(and_28_out));  // open: en, clr
  assign or_14_out = value | and_12_out;  // OR_Gate or_14, 16 bits wide
  and and_28 (and_28_out, write, wrt8);
  Register #(.width(16)) register_10 (.D(or_15_out), .Q(register_10_q), .clk(and_29_out));  // open: en, clr
  assign or_15_out = value | and_13_out;  // OR_Gate or_15, 16 bits wide
  and and_29 (and_29_out, write, wrt9);
  Register #(.width(16)) register_11 (.D(or_16_out), .Q(register_11_q), .clk(and_30_out));  // open: en, clr
  assign or_16_out = value | and_14_out;  // OR_Gate or_16, 16 bits wide
  and and_30 (and_30_out, write, wrt10);
  Register #(.width(16)) register_12 (.D(or_17_out), .Q(register_12_q), .clk(and_31_out));  // open: en, clr
  assign or_17_out = value | and_15_out;  // OR_Gate or_17, 16 bits wide
  and and_31 (and_31_out, write, wrt11);
  assign or_18_out = value | and_16_out;  // OR_Gate or_18, 16 bits wide
  Register #(.width(16)) register_13 (.D(or_18_out), .Q(register_13_q), .clk(and_32_out));  // open: en, clr
  and and_32 (and_32_out, write, wrt12);
  Register #(.width(16)) register_14 (.D(or_19_out), .Q(register_14_q), .clk(and_33_out));  // open: en, clr
  assign or_19_out = value | and_17_out;  // OR_Gate or_19, 16 bits wide
  and and_33 (and_33_out, write, wrt13);
  assign or_20_out = value | and_18_out;  // OR_Gate or_20, 16 bits wide
  Register #(.width(16)) register_15 (.D(or_20_out), .Q(register_15_q), .clk(and_34_out));  // open: en, clr
  and and_34 (and_34_out, write, wrt14);
  Register #(.width(16)) register_16 (.D(or_21_out), .Q(register_16_q), .clk(and_35_out));  // open: en, clr
  assign or_21_out = value | and_19_out;  // OR_Gate or_21, 16 bits wide
  and and_35 (and_35_out, write, wrt15);
  not not_27 (not_27_out, game_over);
  and and_36 (and_36_out, check, wrt0);
  not not_28 (not_28_out, game_over);
  and and_37 (and_37_out, check, wrt1);
  not not_29 (not_29_out, game_over);
  and and_38 (and_38_out, check, wrt2);
  not not_30 (not_30_out, game_over);
  and and_39 (and_39_out, check, wrt3);
  not not_31 (not_31_out, game_over);
  and and_40 (and_40_out, check, wrt4);
  not not_32 (not_32_out, game_over);
  and and_41 (and_41_out, check, wrt5);
  not not_33 (not_33_out, game_over);
  and and_42 (and_42_out, check, wrt6);
  not not_34 (not_34_out, game_over);
  and and_43 (and_43_out, check, wrt7);
  not not_35 (not_35_out, game_over);
  and and_44 (and_44_out, check, wrt8);
  not not_36 (not_36_out, game_over);
  and and_45 (and_45_out, check, wrt9);
  not not_37 (not_37_out, game_over);
  and and_46 (and_46_out, check, wrt10);
  not not_38 (not_38_out, game_over);
  and and_47 (and_47_out, check, wrt11);
  not not_39 (not_39_out, game_over);
  and and_48 (and_48_out, check, wrt12);
  not not_40 (not_40_out, game_over);
  and and_49 (and_49_out, check, wrt13);
  not not_41 (not_41_out, game_over);
  and and_50 (and_50_out, check, wrt14);
  not not_42 (not_42_out, game_over);
  and and_51 (and_51_out, check, wrt15);
  assign controlled_buffer_7_out = not_27_out ? register_1_q : 16'bz;  // Controlled_Buffer controlled_buffer_7
  assign controlled_buffer_7_out = game_over ? end00 : 16'bz;  // Controlled_Buffer controlled_buffer_8
  assign and_52_out = register_1_q & value;  // AND_Gate and_52, 16 bits wide
  assign checked_value = and_36_out ? and_52_out : 16'bz;  // Controlled_Buffer controlled_buffer_9
  assign controlled_buffer_10_out = not_28_out ? register_2_q : 16'bz;  // Controlled_Buffer controlled_buffer_10
  assign controlled_buffer_10_out = game_over ? end01 : 16'bz;  // Controlled_Buffer controlled_buffer_11
  assign checked_value = and_37_out ? and_53_out : 16'bz;  // Controlled_Buffer controlled_buffer_12
  assign and_53_out = register_2_q & value;  // AND_Gate and_53, 16 bits wide
  assign controlled_buffer_13_out = not_29_out ? register_3_q : 16'bz;  // Controlled_Buffer controlled_buffer_13
  assign controlled_buffer_13_out = game_over ? end02 : 16'bz;  // Controlled_Buffer controlled_buffer_14
  assign checked_value = and_38_out ? and_54_out : 16'bz;  // Controlled_Buffer controlled_buffer_15
  assign and_54_out = register_3_q & value;  // AND_Gate and_54, 16 bits wide
  assign controlled_buffer_16_out = game_over ? end03 : 16'bz;  // Controlled_Buffer controlled_buffer_16
  assign controlled_buffer_16_out = not_30_out ? register_4_q : 16'bz;  // Controlled_Buffer controlled_buffer_17
  assign checked_value = and_39_out ? and_55_out : 16'bz;  // Controlled_Buffer controlled_buffer_18
  assign and_55_out = register_4_q & value;  // AND_Gate and_55, 16 bits wide
  assign controlled_buffer_19_out = not_31_out ? register_5_q : 16'bz;  // Controlled_Buffer controlled_buffer_19
  assign controlled_buffer_19_out = game_over ? end04 : 16'bz;  // Controlled_Buffer controlled_buffer_20
  assign and_56_out = register_5_q & value;  // AND_Gate and_56, 16 bits wide
  assign checked_value = and_40_out ? and_56_out : 16'bz;  // Controlled_Buffer controlled_buffer_21
  assign controlled_buffer_22_out = not_32_out ? register_6_q : 16'bz;  // Controlled_Buffer controlled_buffer_22
  assign controlled_buffer_22_out = game_over ? end05 : 16'bz;  // Controlled_Buffer controlled_buffer_23
  assign and_57_out = register_6_q & value;  // AND_Gate and_57, 16 bits wide
  assign checked_value = and_41_out ? and_57_out : 16'bz;  // Controlled_Buffer controlled_buffer_24
  assign controlled_buffer_25_out = game_over ? end06 : 16'bz;  // Controlled_Buffer controlled_buffer_25
  assign controlled_buffer_25_out = not_33_out ? register_7_q : 16'bz;  // Controlled_Buffer controlled_buffer_26
  assign and_58_out = register_7_q & value;  // AND_Gate and_58, 16 bits wide
  assign checked_value = and_42_out ? and_58_out : 16'bz;  // Controlled_Buffer controlled_buffer_27
  assign controlled_buffer_28_out = not_34_out ? register_8_q : 16'bz;  // Controlled_Buffer controlled_buffer_28
  assign controlled_buffer_28_out = game_over ? end07 : 16'bz;  // Controlled_Buffer controlled_buffer_29
  assign checked_value = and_43_out ? and_59_out : 16'bz;  // Controlled_Buffer controlled_buffer_30
  assign and_59_out = register_8_q & value;  // AND_Gate and_59, 16 bits wide
  assign controlled_buffer_31_out = not_35_out ? register_9_q : 16'bz;  // Controlled_Buffer controlled_buffer_31
  assign controlled_buffer_31_out = game_over ? end08 : 16'bz;  // Controlled_Buffer controlled_buffer_32
  assign checked_value = and_44_out ? and_60_out : 16'bz;  // Controlled_Buffer controlled_buffer_33
  assign and_60_out = register_9_q & value;  // AND_Gate and_60, 16 bits wide
  assign controlled_buffer_34_out = game_over ? end09 : 16'bz;  // Controlled_Buffer controlled_buffer_34
  assign controlled_buffer_34_out = not_36_out ? register_10_q : 16'bz;  // Controlled_Buffer controlled_buffer_35
  assign and_61_out = register_10_q & value;  // AND_Gate and_61, 16 bits wide
  assign checked_value = and_45_out ? and_61_out : 16'bz;  // Controlled_Buffer controlled_buffer_36
  assign controlled_buffer_37_out = game_over ? end10 : 16'bz;  // Controlled_Buffer controlled_buffer_37
  assign controlled_buffer_37_out = not_37_out ? register_11_q : 16'bz;  // Controlled_Buffer controlled_buffer_38
  assign and_62_out = register_11_q & value;  // AND_Gate and_62, 16 bits wide
  assign checked_value = and_46_out ? and_62_out : 16'bz;  // Controlled_Buffer controlled_buffer_39
  assign controlled_buffer_40_out = not_38_out ? register_12_q : 16'bz;  // Controlled_Buffer controlled_buffer_40
  assign controlled_buffer_40_out = game_over ? end11 : 16'bz;  // Controlled_Buffer controlled_buffer_41
  assign and_63_out = register_12_q & value;  // AND_Gate and_63, 16 bits wide
  assign checked_value = and_47_out ? and_63_out : 16'bz;  // Controlled_Buffer controlled_buffer_42
  assign controlled_buffer_43_out = not_39_out ? register_13_q : 16'bz;  // Controlled_Buffer controlled_buffer_43
  assign controlled_buffer_43_out = game_over ? end12 : 16'bz;  // Controlled_Buffer controlled_buffer_44
  assign and_64_out = register_13_q & value;  // AND_Gate and_64, 16 bits wide
  assign checked_value = and_48_out ? and_64_out : 16'bz;  // Controlled_Buffer controlled_buffer_45
  assign controlled_buffer_46_out = game_over ? end13 : 16'bz;  // Controlled_Buffer controlled_buffer_46
  assign controlled_buffer_46_out = not_40_out ? register_14_q : 16'bz;  // Controlled_Buffer controlled_buffer_47
  assign and_65_out = register_14_q & value;  // AND_Gate and_65, 16 bits wide
  assign checked_value = and_49_out ? and_65_out : 16'bz;  // Controlled_Buffer controlled_buffer_48
  assign controlled_buffer_49_out = not_41_out ? register_15_q : 16'bz;  // Controlled_Buffer controlled_buffer_49
  assign controlled_buffer_49_out = game_over ? end14 : 16'bz;  // Controlled_Buffer controlled_buffer_50
  assign and_66_out = register_15_q & value;  // AND_Gate and_66, 16 bits wide
  assign checked_value = and_50_out ? and_66_out : 16'bz;  // Controlled_Buffer controlled_buffer_51
  assign controlled_buffer_52_out = not_42_out ? register_16_q : 16'bz;  // Controlled_Buffer controlled_buffer_52
  assign controlled_buffer_52_out = game_over ? end15 : 16'bz;  // Controlled_Buffer controlled_buffer_53
  assign and_67_out = register_16_q & value;  // AND_Gate and_67, 16 bits wide
  assign checked_value = and_51_out ? and_67_out : 16'bz;  // Controlled_Buffer controlled_buffer_54
  not not_43 (not_43_out, start);
  assign controlled_buffer_55_out = start ? beg00 : 16'bz;  // Controlled_Buffer controlled_buffer_55
  assign controlled_buffer_55_out = not_43_out ? controlled_buffer_7_out : 16'bz;  // Controlled_Buffer controlled_buffer_56
  Pull_Resistor pull_resistor_4 (.node(checked_value));
  // Probe on checked_value
  not not_44 (not_44_out, start);
  assign controlled_buffer_57_out = not_44_out ? controlled_buffer_10_out : 16'bz;  // Controlled_Buffer controlled_buffer_57
  assign controlled_buffer_57_out = start ? beg01 : 16'bz;  // Controlled_Buffer controlled_buffer_58
  Pull_Resistor pull_resistor_5 (.node(checked_value));
  // Probe on checked_value
  not not_45 (not_45_out, start);
  assign controlled_buffer_59_out = start ? beg02 : 16'bz;  // Controlled_Buffer controlled_buffer_59
  assign controlled_buffer_59_out = not_45_out ? controlled_buffer_13_out : 16'bz;  // Controlled_Buffer controlled_buffer_60
  Pull_Resistor pull_resistor_6 (.node(checked_value));
  // Probe on checked_value
  not not_46 (not_46_out, start);
  assign controlled_buffer_61_out = not_46_out ? controlled_buffer_16_out : 16'bz;  // Controlled_Buffer controlled_buffer_61
  assign controlled_buffer_61_out = start ? beg03 : 16'bz;  // Controlled_Buffer controlled_buffer_62
  Pull_Resistor pull_resistor_7 (.node(checked_value));
  // Probe on checked_value
  not not_47 (not_47_out, start);
  assign controlled_buffer_63_out = start ? beg04 : 16'bz;  // Controlled_Buffer controlled_buffer_63
  assign controlled_buffer_63_out = not_47_out ? controlled_buffer_19_out : 16'bz;  // Controlled_Buffer controlled_buffer_64
  Pull_Resistor pull_resistor_8 (.node(checked_value));
  // Probe on checked_value
  not not_48 (not_48_out, start);
  assign controlled_buffer_65_out = start ? beg05 : 16'bz;  // Controlled_Buffer controlled_buffer_65
  assign controlled_buffer_65_out = not_48_out ? controlled_buffer_22_out : 16'bz;  // Controlled_Buffer controlled_buffer_66
  Pull_Resistor pull_resistor_9 (.node(checked_value));
  // Probe on checked_value
  not not_49 (not_49_out, start);
  assign controlled_buffer_67_out = start ? beg06 : 16'bz;  // Controlled_Buffer controlled_buffer_67
  assign controlled_buffer_67_out = not_49_out ? controlled_buffer_25_out : 16'bz;  // Controlled_Buffer controlled_buffer_68
  Pull_Resistor pull_resistor_10 (.node(checked_value));
  // Probe on checked_value
  not not_50 (not_50_out, start);
  assign controlled_buffer_69_out = not_50_out ? controlled_buffer_28_out : 16'bz;  // Controlled_Buffer controlled_buffer_69
  assign controlled_buffer_69_out = start ? beg07 : 16'bz;  // Controlled_Buffer controlled_buffer_70
  Pull_Resistor pull_resistor_11 (.node(checked_value));
  // Probe on checked_value
  not not_51 (not_51_out, start);
  assign controlled_buffer_71_out = not_51_out ? controlled_buffer_31_out : 16'bz;  // Controlled_Buffer controlled_buffer_71
  assign controlled_buffer_71_out = start ? beg08 : 16'bz;  // Controlled_Buffer controlled_buffer_72
  Pull_Resistor pull_resistor_12 (.node(checked_value));
  // Probe on checked_value
  not not_52 (not_52_out, start);
  assign controlled_buffer_73_out = not_52_out ? controlled_buffer_34_out : 16'bz;  // Controlled_Buffer controlled_buffer_73
  assign controlled_buffer_73_out = start ? beg09 : 16'bz;  // Controlled_Buffer controlled_buffer_74
  Pull_Resistor pull_resistor_13 (.node(checked_value));
  // Probe on checked_value
  not not_53 (not_53_out, start);
  assign controlled_buffer_75_out = not_53_out ? controlled_buffer_37_out : 16'bz;  // Controlled_Buffer controlled_buffer_75
  assign controlled_buffer_75_out = start ? beg10 : 16'bz;  // Controlled_Buffer controlled_buffer_76
  Pull_Resistor pull_resistor_14 (.node(checked_value));
  // Probe on checked_value
  not not_54 (not_54_out, start);
  assign controlled_buffer_77_out = start ? beg11 : 16'bz;  // Controlled_Buffer controlled_buffer_77
  assign controlled_buffer_77_out = not_54_out ? controlled_buffer_40_out : 16'bz;  // Controlled_Buffer controlled_buffer_78
  Pull_Resistor pull_resistor_15 (.node(checked_value));
  // Probe on checked_value
  not not_55 (not_55_out, start);
  assign controlled_buffer_79_out = start ? beg12 : 16'bz;  // Controlled_Buffer controlled_buffer_79
  assign controlled_buffer_79_out = not_55_out ? controlled_buffer_43_out : 16'bz;  // Controlled_Buffer controlled_buffer_80
  Pull_Resistor pull_resistor_16 (.node(checked_value));
  // Probe on checked_value
  not not_56 (not_56_out, start);
  assign controlled_buffer_81_out = start ? beg13 : 16'bz;  // Controlled_Buffer controlled_buffer_81
  assign controlled_buffer_81_out = not_56_out ? controlled_buffer_46_out : 16'bz;  // Controlled_Buffer controlled_buffer_82
  Pull_Resistor pull_resistor_17 (.node(checked_value));
  // Probe on checked_value
  not not_57 (not_57_out, start);
  assign controlled_buffer_83_out = not_57_out ? controlled_buffer_49_out : 16'bz;  // Controlled_Buffer controlled_buffer_83
  assign controlled_buffer_83_out = start ? beg14 : 16'bz;  // Controlled_Buffer controlled_buffer_84
  Pull_Resistor pull_resistor_18 (.node(checked_value));
  // Probe on checked_value
  not not_58 (not_58_out, start);
  assign controlled_buffer_85_out = not_58_out ? controlled_buffer_52_out : 16'bz;  // Controlled_Buffer controlled_buffer_85
  assign controlled_buffer_85_out = start ? beg15 : 16'bz;  // Controlled_Buffer controlled_buffer_86
  Pull_Resistor pull_resistor_19 (.node(checked_value));
  // Probe on checked_value
  not not_59 (not_59_out, victory);
  assign c00 = victory ? win00 : 16'bz;  // Controlled_Buffer controlled_buffer_87
  assign c00 = not_59_out ? controlled_buffer_55_out : 16'bz;  // Controlled_Buffer controlled_buffer_88
  not not_60 (not_60_out, victory);
  assign c01 = not_60_out ? controlled_buffer_57_out : 16'bz;  // Controlled_Buffer controlled_buffer_89
  assign c01 = victory ? win01 : 16'bz;  // Controlled_Buffer controlled_buffer_90
  not not_61 (not_61_out, victory);
  assign c02 = not_61_out ? controlled_buffer_59_out : 16'bz;  // Controlled_Buffer controlled_buffer_91
  assign c02 = victory ? win02 : 16'bz;  // Controlled_Buffer controlled_buffer_92
  not not_62 (not_62_out, victory);
  assign c03 = victory ? win03 : 16'bz;  // Controlled_Buffer controlled_buffer_93
  assign c03 = not_62_out ? controlled_buffer_61_out : 16'bz;  // Controlled_Buffer controlled_buffer_94
  not not_63 (not_63_out, victory);
  assign c04 = victory ? win04 : 16'bz;  // Controlled_Buffer controlled_buffer_95
  assign c04 = not_63_out ? controlled_buffer_63_out : 16'bz;  // Controlled_Buffer controlled_buffer_96
  not not_64 (not_64_out, victory);
  assign c05 = not_64_out ? controlled_buffer_65_out : 16'bz;  // Controlled_Buffer controlled_buffer_97
  assign c05 = victory ? win05 : 16'bz;  // Controlled_Buffer controlled_buffer_98
  not not_65 (not_65_out, victory);
  assign c06 = victory ? win06 : 16'bz;  // Controlled_Buffer controlled_buffer_99
  assign c06 = not_65_out ? controlled_buffer_67_out : 16'bz;  // Controlled_Buffer controlled_buffer_100
  not not_66 (not_66_out, victory);
  assign c07 = not_66_out ? controlled_buffer_69_out : 16'bz;  // Controlled_Buffer controlled_buffer_101
  assign c07 = victory ? win07 : 16'bz;  // Controlled_Buffer controlled_buffer_102
  not not_67 (not_67_out, victory);
  assign c08 = victory ? win08 : 16'bz;  // Controlled_Buffer controlled_buffer_103
  assign c08 = not_67_out ? controlled_buffer_71_out : 16'bz;  // Controlled_Buffer controlled_buffer_104
  not not_68 (not_68_out, victory);
  assign c09 = victory ? win09 : 16'bz;  // Controlled_Buffer controlled_buffer_105
  assign c09 = not_68_out ? controlled_buffer_73_out : 16'bz;  // Controlled_Buffer controlled_buffer_106
  not not_69 (not_69_out, victory);
  assign c10 = not_69_out ? controlled_buffer_75_out : 16'bz;  // Controlled_Buffer controlled_buffer_107
  assign c10 = victory ? win10 : 16'bz;  // Controlled_Buffer controlled_buffer_108
  not not_70 (not_70_out, victory);
  assign c11 = not_70_out ? controlled_buffer_77_out : 16'bz;  // Controlled_Buffer controlled_buffer_109
  assign c11 = victory ? win11 : 16'bz;  // Controlled_Buffer controlled_buffer_110
  not not_71 (not_71_out, victory);
  assign c12 = not_71_out ? controlled_buffer_79_out : 16'bz;  // Controlled_Buffer controlled_buffer_111
  assign c12 = victory ? win12 : 16'bz;  // Controlled_Buffer controlled_buffer_112
  not not_72 (not_72_out, victory);
  assign c13 = victory ? win13 : 16'bz;  // Controlled_Buffer controlled_buffer_113
  assign c13 = not_72_out ? controlled_buffer_81_out : 16'bz;  // Controlled_Buffer controlled_buffer_114
  not not_73 (not_73_out, victory);
  assign c14 = not_73_out ? controlled_buffer_83_out : 16'bz;  // Controlled_Buffer controlled_buffer_115
  assign c14 = victory ? win14 : 16'bz;  // Controlled_Buffer controlled_buffer_116
  not not_74 (not_74_out, victory);
  assign c15 = not_74_out ? controlled_buffer_85_out : 16'bz;  // Controlled_Buffer controlled_buffer_117
  assign c15 = victory ? win15 : 16'bz;  // Controlled_Buffer controlled_buffer_118

  // Other names for the same wires on the sheet: end = game_over; x_rand[3:0] = food[3:0]; y_rand[3:0] = food[7:4];
  //   rand_req = req_rand; win = victory

  // Notes on the sheet:
  //   VICTORY screen
  //   START screen
  //   GAME OVER screen
endmodule

module reverser (
  input  [15:0] in,
  output [15:0] reversed
);


  assign reversed = {in[0], in[1], in[2], in[3], in[4], in[5], in[6], in[7], in[8], in[9], in[10], in[11], in[12], in[13], in[14], in[15]};
endmodule
