// Logisim project display-decoder.circ as structural Verilog: 1 circuit, main circuit decoder
module decoder (
  input  [15:0] in_1,
  output [3:0] X_coord__bits_0_3,
  output [3:0] Y_coord__bits_4_7,
  output pixel_state__bit_8,
  output write__bit_9
);


  assign pixel_state__bit_8 = in_1[8];
  assign write__bit_9 = in_1[9];
  assign X_coord__bits_0_3 = in_1[3:0];
  assign Y_coord__bits_4_7 = in_1[7:4];
endmodule
