// Logisim project main.circ as structural Verilog: 5 circuits, main circuit main
module main (
  input  bus_0,
  input  bus_0_2
);

  wire check_collision, clock_1_out, clock_2_out, collision, decoder_1_pixel_state__bit_8,
       decoder_1_write__bit_9, game_over, inc, random_req, win;
  wire [3:0] counter_2_out_4, counter_2_out_5, counter_2_out_6, current_direction,
       decoder_1_x_coord__bits_0_3, decoder_1_y_coord__bits_4_7, keyboard;
  wire [6:0] keyboard_1_data;
  wire [7:0] food;
  wire [15:0] display, display_controller_1_p5, display_controller_1_p6, display_controller_1_p8,
       display_controller_1_p9, display_controller_1_p11, display_controller_1_p12, display_controller_1_p13,
       display_controller_1_p14, display_controller_1_p15, display_controller_1_p17,
       display_controller_1_p18, display_controller_1_p19, display_controller_1_p20,
       display_controller_1_p21, display_controller_1_p23, display_controller_1_p24;

  // Debugger debugger_1: pin names not known
  computer computer_1 (
    .keyboard(keyboard), .display(display), .collision(collision), .check_collision(check_collision),
    .game_over(game_over), .inc_score(inc), .random_req(random_req), .random_get(food), .win(win),
    .current_direction(current_direction));
  decoder decoder_1 (
    .in_1(display), .X_coord__bits_0_3(decoder_1_x_coord__bits_0_3),
    .Y_coord__bits_4_7(decoder_1_y_coord__bits_4_7), .pixel_state__bit_8(decoder_1_pixel_state__bit_8),
    .write__bit_9(decoder_1_write__bit_9));
  Clock clock_1 (.out(clock_1_out));
  DotMatrix #(.matrixcols(16), .matrixrows(16)) dotmatrix_1 (
    .col0(display_controller_1_p5), .col1(display_controller_1_p6), .col2(display_controller_1_p8),
    .col3(display_controller_1_p9), .col4(display_controller_1_p11), .col5(display_controller_1_p12),
    .col6(display_controller_1_p13), .col7(display_controller_1_p14), .col8(display_controller_1_p15),
    .col9(display_controller_1_p17), .col10(display_controller_1_p18), .col11(display_controller_1_p19),
    .col12(display_controller_1_p20), .col13(display_controller_1_p21), .col14(display_controller_1_p23),
    .col15(display_controller_1_p24));
  // display_controller display_controller_1: pin names not known; wires that end beside it: decoder_1_x_coord__bits_0_3, decoder_1_y_coord__bits_4_7, decoder_1_pixel_state__bit_8, decoder_1_write__bit_9, display_controller_1_p5, display_controller_1_p6, check_collision, display_controller_1_p8, display_controller_1_p9, collision, display_controller_1_p11, display_controller_1_p12, display_controller_1_p13, display_controller_1_p14, display_controller_1_p15, random_req, display_controller_1_p17, display_controller_1_p18, display_controller_1_p19, display_controller_1_p20, display_controller_1_p21, game_over, display_controller_1_p23, display_controller_1_p24, win, food
  Clock clock_2 (.out(clock_2_out));
  Keyboard keyboard_1 (.clk(clock_2_out), .data(keyboard_1_data));  // open: re, clr, avail
  Counter counter_1 (.load(bus_0), .D(8'h80), .count(bus_0_2), .clk(clock_1_out));  // open: Q, carry, clr
  keyboard_decoder keyboard_decoder_1 (
    .keyboard_input(keyboard_1_data), .keyboard_output(keyboard), .current_direction(current_direction));
  // Probe on keyboard
  Hex_Digit_Display hex_digit_display_1 (.value(counter_2_out_4));  // open: dp
  counter counter_2 (
    .increment(inc), .out_4(counter_2_out_4), .out_5(counter_2_out_5), .out_6(counter_2_out_6),
    .target_score(16'h8), .victory(win));  // open: zero
  Hex_Digit_Display hex_digit_display_2 (.value(counter_2_out_6));  // open: dp
  Hex_Digit_Display hex_digit_display_3 (.value(counter_2_out_5));  // open: dp

  // Notes on the sheet:
  //   Тут мы ставим кнопки для управления змеёй
  //   Тут мы ставим счётчик
endmodule

module memory_map_extrude (
  input  [15:0] addr,
  input  [15:0] constant,
  input  store_start_address,
  output [3:0] out_4,
  output map_active
);

  wire and_1_out, and_2_out, and_4_out, and_5_out, and_6_out, clock_1_out, multiplexer_2_out,
       multiplexer_3_out, not_1_out, not_2_out, not_3_out, not_4_out, not_5_out, not_6_out, t_ff_1_q,
       t_ff_1_qn;
  wire [11:0] xnor_1_out;
  wire [15:0] multiplexer_1_out, register_1_q;
  wire [15:4] subtractor_1_out;

  Multiplexer #(.width(16)) multiplexer_1 (
    .in0(constant), .in1(16'h8000), .out(multiplexer_1_out), .sel(not_1_out));  // open: en
  not not_1 (not_1_out, not_2_out);
  not not_2 (not_2_out, not_3_out);
  not not_3 (not_3_out, not_4_out);
  not not_4 (not_4_out, not_5_out);
  not not_5 (not_5_out, store_start_address);
  Register #(.width(16)) register_1 (.D(multiplexer_1_out), .Q(register_1_q), .clk(and_1_out));  // open: en, clr
  and and_1 (and_1_out, not_5_out, multiplexer_2_out);
  Multiplexer multiplexer_2 (
    .in0(store_start_address), .in1(multiplexer_3_out), .out(multiplexer_2_out), .sel(not_5_out));  // open: en
  Subtractor #(.width(16)) subtractor_1 (
    .a(addr), .b(register_1_q), .out({subtractor_1_out, out_4}));  // open: bin, bout
  Multiplexer multiplexer_3 (.in0(not_6_out), .in1(1'b0), .out(multiplexer_3_out), .sel(t_ff_1_q));  // open: en
  T_Flip_Flop t_ff_1 (
    .clk(store_start_address), .T(t_ff_1_qn), .Q(t_ff_1_q), .Qn(t_ff_1_qn));  // open: preset, reset, en
  not not_6 (not_6_out, clock_1_out);
  Clock clock_1 (.out(clock_1_out));
  assign xnor_1_out = ~(subtractor_1_out ^ {12{1'b0}});  // XNOR_Gate xnor_1, 12 bits wide
  and and_2 (and_2_out, xnor_1_out[11], xnor_1_out[10], xnor_1_out[9]);
  and and_3 (map_active, and_2_out, and_4_out, and_5_out, and_6_out);
  and and_4 (and_4_out, xnor_1_out[8], xnor_1_out[7], xnor_1_out[6]);
  and and_5 (and_5_out, xnor_1_out[5], xnor_1_out[4], xnor_1_out[3]);
  and and_6 (and_6_out, xnor_1_out[2], xnor_1_out[1], xnor_1_out[0]);
endmodule

module random_generator (
  input  get_random,
  output [15:0] random_XY
);

  wire [7:0] random_1_out;

  Random #(.trigger("falling")) random_1 (.clk(get_random), .out(random_1_out));  // open: next, clr
  assign random_XY = {{8{1'b0}}, random_1_out};  // Bit_Extender bit_extender_1
endmodule

module keyboard_decoder (
  input  [6:0] keyboard_input,
  input  [3:0] current_direction,
  output [3:0] keyboard_output
);

  wire and_1_out, clock_1_out, or_1_out;
  wire [3:0] not_1_out, not_2_out, out, transistor_1_out;

  Transistor transistor_1 (.in(out[0]), .out(transistor_1_out[0]), .gate(current_direction[2]));
  Transistor transistor_2 (.in(out[1]), .out(transistor_1_out[1]), .gate(current_direction[3]));
  Transistor transistor_3 (.in(out[2]), .out(transistor_1_out[2]), .gate(current_direction[0]));
  Transistor transistor_4 (.in(out[3]), .out(transistor_1_out[3]), .gate(current_direction[1]));
  Comparator #(.width(7)) comparator_1 (.a(keyboard_input), .b(7'b1110111), .eq(out[0]));  // open: gt, lt
  Comparator #(.width(7)) comparator_2 (.a(keyboard_input), .b(7'b1100100), .eq(out[1]));  // open: gt, lt
  Comparator #(.width(7)) comparator_3 (.a(keyboard_input), .b(7'b1110011), .eq(out[2]));  // open: gt, lt
  Comparator #(.width(7)) comparator_4 (.a(keyboard_input), .b(7'b1100001), .eq(out[3]));  // open: gt, lt
  Pull_Resistor pull_resistor_1 (.node(transistor_1_out));
  assign not_1_out = ~not_2_out;  // NOT_Gate not_1, 4 bits wide
  assign not_2_out = ~transistor_1_out;  // NOT_Gate not_2, 4 bits wide
  or or_1 (or_1_out, transistor_1_out[0], transistor_1_out[1], transistor_1_out[3], transistor_1_out[2]);
  and and_1 (and_1_out, or_1_out, clock_1_out);
  Clock clock_1 (.out(clock_1_out));
  Register #(.width(4)) register_1 (.D(not_1_out), .Q(keyboard_output), .clk(and_1_out));  // open: en, clr
endmodule

module computer (
  input  collision,
  input  [3:0] keyboard,
  input  [7:0] random_get,
  input  win,
  output [3:0] current_direction,
  output random_req,
  output check_collision,
  output [15:0] display,
  output game_over,
  output inc_score
);

  wire and_1_out, and_2_out, cdm_16_1_p3, cdm_16_1_p7, clock_2_out, clock_3_out, code, mem_sel, memdata,
       memory, memory_map_extrude_1_map_active, not_1_out, read_write, store_start_address, word;
  wire [3:0] memory_map_extrude_1_out_4;
  wire [15:0] address, cdm_16_1_p4, cdm_16_1_p12, cdm_16_1_p13, data, multiplexer_1_out, s00, s01, s02, s03,
       s04, s05, s06, s07, s08, s09, s10, s11, s12, s13, s14, s15, start_address;
  wire [15:5] cdm_16_1_p6;

  // Probe on display
  // CdM_16 cdm_16_1: pin names not known; wires that end beside it: win, display, cdm_16_1_p3, cdm_16_1_p4, start_address, {cdm_16_1_p6, inc_score, store_start_address, game_over, check_collision, random_req}, cdm_16_1_p7, memory, read_write, word, address, cdm_16_1_p12, cdm_16_1_p13
  Clock clock_1 (.out(cdm_16_1_p3));
  // Debugger debugger_1: pin names not known
  Bit_Extender #(.in_width(16), .out_width(4)) bit_extender_1 (.in(cdm_16_1_p4), .out(current_direction));
  assign data = not_1_out ? cdm_16_1_p12 : 16'bz;  // Controlled_Buffer controlled_buffer_1
  not not_1 (not_1_out, read_write);
  assign cdm_16_1_p13 = read_write ? data : 16'bz;  // Controlled_Buffer controlled_buffer_2
  Decoder decoder_1 (.out0(code), .out1(memdata), .sel(cdm_16_1_p7), .en(memory));
  // Probe on start_address
  Pull_Resistor pull_resistor_1 (.node(code));
  Pull_Resistor pull_resistor_2 (.node(memdata));
  Clock clock_2 (.out(clock_2_out));
  // Probe on address
  not not_2 (mem_sel, and_1_out);
  and and_1 (and_1_out, read_write, clock_2_out, memory_map_extrude_1_map_active);
  memory_map_extrude memory_map_extrude_1 (
    .addr(address), .constant(start_address), .out_4(memory_map_extrude_1_out_4),
    .store_start_address(store_start_address), .map_active(memory_map_extrude_1_map_active));
  // ROM rom_1: pin names not known; wires that end beside it: address, code, word, data
  and and_2 (and_2_out, memdata, mem_sel);
  Clock clock_3 (.out(clock_3_out));
  assign data = and_1_out ? multiplexer_1_out : 16'bz;  // Controlled_Buffer controlled_buffer_3
  Multiplexer #(.select(4), .width(16)) multiplexer_1 (
    .in0(s00), .in1(s01), .in2(s02), .in3(s03), .in4(s04), .in5(s05), .in6(s06), .in7(s07), .in8(s08),
    .in9(s09), .in10(s10), .in11(s11), .in12(s12), .in13(s13), .in14(s14), .in15(s15),
    .out(multiplexer_1_out), .sel(memory_map_extrude_1_out_4), .en(1'b1));
  // RAM ram_1: pin names not known; wires that end beside it: address, word, and_2_out, clock_3_out, read_write, data
  assign s02 = {{15{1'b0}}, collision};  // Bit_Extender bit_extender_2
  assign s00 = {{12{1'b0}}, keyboard};  // Bit_Extender bit_extender_3
  assign s01 = {{8{1'b0}}, random_get};  // Bit_Extender bit_extender_4
endmodule
