// Logisim project one_pixel_circ.circ as structural Verilog: 2 circuits, main circuit main
module main (
);

  wire cdm_16_1_p1, cdm_16_1_p2, cdm_16_1_p3, cdm_16_1_p7, cdm_16_1_p8, cdm_16_1_p9, cdm_16_1_p10,
       clock_2_out, clock_3_out, not_1_out, not_2_out;
  wire [3:0] bit_extender_1_out, bit_extender_2_out;
  wire [15:0] cdm_16_1_p4, cdm_16_1_p5, cdm_16_1_p11, cdm_16_1_p12, controlled_buffer_1_out,
       display_controller_1_c0, display_controller_1_c1, display_controller_1_c2, display_controller_1_c3,
       display_controller_1_c4, display_controller_1_c5, display_controller_1_c6, display_controller_1_c7,
       display_controller_1_c8, display_controller_1_c9, display_controller_1_c10, display_controller_1_c11,
       display_controller_1_c12, display_controller_1_c13, display_controller_1_c14, display_controller_1_c15;

  // Probe on cdm_16_1_p2
  // Probe on cdm_16_1_p1
  // CdM_16 cdm_16_1: pin names not known; wires that end beside it: cdm_16_1_p1, cdm_16_1_p2, cdm_16_1_p3, cdm_16_1_p4, cdm_16_1_p5, cdm_16_1_p5, cdm_16_1_p7, cdm_16_1_p8, cdm_16_1_p9, cdm_16_1_p10, cdm_16_1_p11, cdm_16_1_p12
  Clock clock_1 (.out(cdm_16_1_p3));
  Bit_Extender #(.in_width(16), .out_width(4)) bit_extender_1 (.in(cdm_16_1_p4), .out(bit_extender_1_out));
  // Probe on cdm_16_1_p4
  // Probe on cdm_16_1_p5
  Bit_Extender #(.in_width(16), .out_width(4)) bit_extender_2 (.in(cdm_16_1_p5), .out(bit_extender_2_out));
  assign controlled_buffer_1_out = not_1_out ? cdm_16_1_p11 : 16'bz;  // Controlled_Buffer controlled_buffer_1
  not not_1 (not_1_out, cdm_16_1_p8);
  assign cdm_16_1_p12 = cdm_16_1_p8 ? controlled_buffer_1_out : 16'bz;  // Controlled_Buffer controlled_buffer_2
  not not_2 (not_2_out, cdm_16_1_p4[4]);
  Button button ();  // open: out
  Button v ();  // open: out
  Button button_2 ();  // open: out
  DotMatrix #(.matrixcols(16), .matrixrows(16)) dotmatrix_1 (
    .col0(display_controller_1_c0), .col1(display_controller_1_c1), .col2(display_controller_1_c2),
    .col3(display_controller_1_c3), .col4(display_controller_1_c4), .col5(display_controller_1_c5),
    .col6(display_controller_1_c6), .col7(display_controller_1_c7), .col8(display_controller_1_c8),
    .col9(display_controller_1_c9), .col10(display_controller_1_c10), .col11(display_controller_1_c11),
    .col12(display_controller_1_c12), .col13(display_controller_1_c13), .col14(display_controller_1_c14),
    .col15(display_controller_1_c15));
  display_controller display_controller_1 (
    .X_coord(bit_extender_1_out), .Y_coord(bit_extender_2_out), .pixel_state(not_2_out), .write(clock_2_out),
    .c0(display_controller_1_c0), .c1(display_controller_1_c1), .c2(display_controller_1_c2),
    .c3(display_controller_1_c3), .c4(display_controller_1_c4), .c5(display_controller_1_c5),
    .c6(display_controller_1_c6), .c7(display_controller_1_c7), .c8(display_controller_1_c8),
    .c9(display_controller_1_c9), .c10(display_controller_1_c10), .c11(display_controller_1_c11),
    .c12(display_controller_1_c12), .c13(display_controller_1_c13), .c14(display_controller_1_c14),
    .c15(display_controller_1_c15));
  Clock clock_2 (.out(clock_2_out));
  Clock clock_3 (.out(clock_3_out));
  Button button_3 ();  // open: out
  // RAM ram_1: pin names not known; wires that end beside it: cdm_16_1_p10, cdm_16_1_p9, cdm_16_1_p7, clock_3_out, cdm_16_1_p8, controlled_buffer_1_out
endmodule

module display_controller (
  input  [3:0] X_coord,
  input  [3:0] Y_coord,
  input  pixel_state,
  input  write,
  output [15:0] c0,
  output [15:0] c1,
  output [15:0] c2,
  output [15:0] c3,
  output [15:0] c4,
  output [15:0] c5,
  output [15:0] c6,
  output [15:0] c7,
  output [15:0] c8,
  output [15:0] c9,
  output [15:0] c10,
  output [15:0] c11,
  output [15:0] c12,
  output [15:0] c13,
  output [15:0] c14,
  output [15:0] c15
);

  wire wrt0, wrt1, wrt2, wrt3, wrt4, wrt5, wrt6, wrt7, wrt8, wrt9, wrt10, wrt11, wrt12, wrt13, wrt14, wrt15;
  wire [15:0] and_1_out, and_2_out, and_3_out, and_4_out, and_5_out, and_6_out, and_7_out, and_8_out,
       and_9_out, and_10_out, and_11_out, and_12_out, and_13_out, and_14_out, and_15_out, and_16_out,
       demultiplexer_3_out0, mask, or_1_out, or_2_out, or_3_out, or_4_out, or_5_out, or_6_out, or_7_out,
       or_8_out, or_9_out, or_10_out, or_11_out, or_12_out, or_13_out, or_14_out, or_15_out, or_16_out, value;

  Demultiplexer #(.select(4)) demultiplexer_1 (
    .out0(wrt0), .out1(wrt1), .out2(wrt2), .out3(wrt3), .out4(wrt4), .out5(wrt5), .out6(wrt6), .out7(wrt7),
    .out8(wrt8), .out9(wrt9), .out10(wrt10), .out11(wrt11), .out12(wrt12), .out13(wrt13), .out14(wrt14),
    .out15(wrt15), .in(write), .sel(X_coord));  // open: en
  Demultiplexer #(.select(4)) demultiplexer_2 (
    .out0(value[0]), .out1(value[1]), .out2(value[2]), .out3(value[3]), .out4(value[4]), .out5(value[5]),
    .out6(value[6]), .out7(value[7]), .out8(value[8]), .out9(value[9]), .out10(value[10]), .out11(value[11]),
    .out12(value[12]), .out13(value[13]), .out14(value[14]), .out15(value[15]), .in(pixel_state),
    .sel(Y_coord));  // open: en
  Demultiplexer #(.select(4)) demultiplexer_3 (
    .out0(demultiplexer_3_out0[0]), .out1(demultiplexer_3_out0[1]), .out2(demultiplexer_3_out0[2]),
    .out3(demultiplexer_3_out0[3]), .out4(demultiplexer_3_out0[4]), .out5(demultiplexer_3_out0[5]),
    .out6(demultiplexer_3_out0[6]), .out7(demultiplexer_3_out0[7]), .out8(demultiplexer_3_out0[8]),
    .out9(demultiplexer_3_out0[9]), .out10(demultiplexer_3_out0[10]), .out11(demultiplexer_3_out0[11]),
    .out12(demultiplexer_3_out0[12]), .out13(demultiplexer_3_out0[13]), .out14(demultiplexer_3_out0[14]),
    .out15(demultiplexer_3_out0[15]), .in(1'b1), .sel(Y_coord));  // open: en
  // Probe on value
  // Probe on mask
  assign mask = ~demultiplexer_3_out0;  // NOT_Gate not_1, 16 bits wide
  assign or_1_out = value | and_1_out;  // OR_Gate or_1, 16 bits wide
  assign and_1_out = c0 & mask;  // AND_Gate and_1, 16 bits wide
  assign or_2_out = value | and_2_out;  // OR_Gate or_2, 16 bits wide
  assign and_2_out = c1 & mask;  // AND_Gate and_2, 16 bits wide
  assign or_3_out = value | and_3_out;  // OR_Gate or_3, 16 bits wide
  assign and_3_out = c2 & mask;  // AND_Gate and_3, 16 bits wide
  assign or_4_out = value | and_4_out;  // OR_Gate or_4, 16 bits wide
  assign and_4_out = c3 & mask;  // AND_Gate and_4, 16 bits wide
  assign or_5_out = value | and_5_out;  // OR_Gate or_5, 16 bits wide
  assign and_5_out = c4 & mask;  // AND_Gate and_5, 16 bits wide
  assign or_6_out = value | and_6_out;  // OR_Gate or_6, 16 bits wide
  assign and_6_out = c5 & mask;  // AND_Gate and_6, 16 bits wide
  assign or_7_out = value | and_7_out;  // OR_Gate or_7, 16 bits wide
  assign and_7_out = c6 & mask;  // AND_Gate and_7, 16 bits wide
  assign or_8_out = value | and_8_out;  // OR_Gate or_8, 16 bits wide
  assign and_8_out = c7 & mask;  // AND_Gate and_8, 16 bits wide
  assign or_9_out = value | and_9_out;  // OR_Gate or_9, 16 bits wide
  assign and_9_out = c8 & mask;  // AND_Gate and_9, 16 bits wide
  assign or_10_out = value | and_10_out;  // OR_Gate or_10, 16 bits wide
  assign and_10_out = c9 & mask;  // AND_Gate and_10, 16 bits wide
  assign or_11_out = value | and_11_out;  // OR_Gate or_11, 16 bits wide
  assign and_11_out = c10 & mask;  // AND_Gate and_11, 16 bits wide
  assign or_12_out = value | and_12_out;  // OR_Gate or_12, 16 bits wide
  assign and_12_out = c11 & mask;  // AND_Gate and_12, 16 bits wide
  assign or_13_out = value | and_13_out;  // OR_Gate or_13, 16 bits wide
  assign and_13_out = c12 & mask;  // AND_Gate and_13, 16 bits wide
  assign or_14_out = value | and_14_out;  // OR_Gate or_14, 16 bits wide
  assign and_14_out = c13 & mask;  // AND_Gate and_14, 16 bits wide
  assign or_15_out = value | and_15_out;  // OR_Gate or_15, 16 bits wide
  assign and_15_out = c14 & mask;  // AND_Gate and_15, 16 bits wide
  assign or_16_out = value | and_16_out;  // OR_Gate or_16, 16 bits wide
  assign and_16_out = c15 & mask;  // AND_Gate and_16, 16 bits wide
  Register #(.width(16)) register_1 (.D(or_1_out), .Q(c0), .clk(wrt0));  // open: en, clr
  Register #(.width(16)) register_2 (.D(or_2_out), .Q(c1), .clk(wrt1));  // open: en, clr
  Register #(.width(16)) register_3 (.D(or_3_out), .Q(c2), .clk(wrt2));  // open: en, clr
  Register #(.width(16)) register_4 (.D(or_4_out), .Q(c3), .clk(wrt3));  // open: en, clr
  Register #(.width(16)) register_5 (.D(or_5_out), .Q(c4), .clk(wrt4));  // open: en, clr
  Register #(.width(16)) register_6 (.D(or_6_out), .Q(c5), .clk(wrt5));  // open: en, clr
  Register #(.width(16)) register_7 (.D(or_7_out), .Q(c6), .clk(wrt6));  // open: en, clr
  Register #(.width(16)) register_8 (.D(or_8_out), .Q(c7), .clk(wrt7));  // open: en, clr
  Register #(.width(16)) register_9 (.D(or_9_out), .Q(c8), .clk(wrt8));  // open: en, clr
  Register #(.width(16)) register_10 (.D(or_10_out), .Q(c9), .clk(wrt9));  // open: en, clr
  Register #(.width(16)) register_11 (.D(or_11_out), .Q(c10), .clk(wrt10));  // open: en, clr
  Register #(.width(16)) register_12 (.D(or_12_out), .Q(c11), .clk(wrt11));  // open: en, clr
  Register #(.width(16)) register_13 (.D(or_13_out), .Q(c12), .clk(wrt12));  // open: en, clr
  Register #(.width(16)) register_14 (.D(or_14_out), .Q(c13), .clk(wrt13));  // open: en, clr
  Register #(.width(16)) register_15 (.D(or_15_out), .Q(c14), .clk(wrt14));  // open: en, clr
  Register #(.width(16)) register_16 (.D(or_16_out), .Q(c15), .clk(wrt15));  // open: en, clr
endmodule
